// Logisim project RV32Idatapath.circ as structural Verilog: 24 circuits, main circuit main
module main (
  input  [11:0] in_1,
  input  [11:0] in_2,
  input  in_3,
  output [31:0] out_4
);

  wire branch_1_out_4, clock_1_out, control_1_out_2, control_1_out_4, control_1_out_6, control_1_out_8,
       control_1_out_9, control_1_out_10;
  wire [1:0] control_1_out_3, control_1_out_5, control_1_out_7;
  wire [2:0] control_1_out_11, control_1_out_12, control_1_out_13, control_1_out_14;
  wire [11:0] alu_1_out_6, multiplexer_1_out, multiplexer_2_out, n4_1_out_3, pc_1_out_3;
  wire [31:0] bit_extender_1_out, bit_extender_2_out, imm_gener_1_out_3, load_1_out_3, multiplexer_3_out,
       multiplexer_4_out, ram_1_data, regfile_1_out_7, regfile_1_out_8, rom_1_data, store_1_out_3;
  wire [31:12] alu_1_out_6_2;

  Multiplexer #(.width(12), .enable("false")) multiplexer_1 (
    .in0(n4_1_out_3), .in1(alu_1_out_6), .out(multiplexer_1_out), .sel(branch_1_out_4));
  Multiplexer #(.select(2), .width(12), .enable("false")) multiplexer_2 (
    .in0(n4_1_out_3), .in1(multiplexer_1_out), .in3(alu_1_out_6), .out(multiplexer_2_out),
    .sel(control_1_out_3));  // open: in2
  control control_1 (
    .in_1(rom_1_data), .out_2(control_1_out_2), .out_8(control_1_out_8), .out_9(control_1_out_9),
    .out_10(control_1_out_10), .out_5(control_1_out_5), .out_3(control_1_out_3), .out_7(control_1_out_7),
    .out_12(control_1_out_12), .out_13(control_1_out_13), .out_11(control_1_out_11),
    .out_14(control_1_out_14), .out_6(control_1_out_6), .out_4(control_1_out_4));
  _4 u_4_1 (.in_1(in_1), .out_3(n4_1_out_3), .in_2(pc_1_out_3));
  PC pc_1 (.in_1(multiplexer_2_out), .in_2(clock_1_out), .out_3(pc_1_out_3));
  ROM #(.addrWidth(12), .dataWidth(32)) rom_1 (.addr(pc_1_out_3), .data(rom_1_data));  // open: sel
  imm_Gener imm_gener_1 (.out_3(imm_gener_1_out_3), .in_2(control_1_out_5), .in_1(rom_1_data));
  assign bit_extender_1_out = {{20{1'b0}}, n4_1_out_3};  // Bit_Extender bit_extender_1
  RegFile regfile_1 (
    .in_1(out_4), .out_7(regfile_1_out_7), .out_8(regfile_1_out_8), .Reg_En(control_1_out_2),
    .dest(rom_1_data[11:7]), .rs2(rom_1_data[24:20]), .rs1(rom_1_data[19:15]), .in_2(clock_1_out));
  Clock clock_1 (.out(clock_1_out));
  branch branch_1 (.in_1(regfile_1_out_7), .in_2(regfile_1_out_8), .out_4(branch_1_out_4), .in_3(control_1_out_14));
  assign bit_extender_2_out = {{20{1'b0}}, pc_1_out_3};  // Bit_Extender bit_extender_2
  Multiplexer #(.width(32), .enable("false")) multiplexer_3 (
    .in0(regfile_1_out_7), .in1(bit_extender_2_out), .out(multiplexer_3_out), .sel(control_1_out_9));
  Multiplexer #(.width(32), .enable("false")) multiplexer_4 (
    .in0(regfile_1_out_8), .in1(imm_gener_1_out_3), .out(multiplexer_4_out), .sel(control_1_out_8));
  ALU alu_1 (
    .in_1(multiplexer_4_out), .in_2(multiplexer_3_out), .in_5(control_1_out_11),
    .out_6({alu_1_out_6_2, alu_1_out_6}), .selectbot_for_add_or_sub(control_1_out_6),
    .srl___sra(control_1_out_4));
  Store store_1 (.in_1(regfile_1_out_8), .in_2(control_1_out_13), .out_3(store_1_out_3));
  Load load_1 (.in_1(ram_1_data), .out_3(load_1_out_3), .in_2(control_1_out_12));
  RAM #(.addrWidth(12), .dataWidth(32), .bus("separate")) ram_1 (
    .addr(alu_1_out_6), .din(store_1_out_3), .data(ram_1_data), .str(control_1_out_10), .sel(1'b1),
    .clk(clock_1_out));  // open: ld, clr
  Multiplexer #(.select(2), .width(32), .enable("false")) multiplexer_5 (
    .in0({alu_1_out_6_2, alu_1_out_6}), .in1(load_1_out_3), .in2(bit_extender_1_out),
    .in3(imm_gener_1_out_3), .out(out_4), .sel(control_1_out_7));

  // Notes on the sheet:
  //   contents of rom_1 (hex, n*v repeats v):
  //   9000093 1081b3 40118233 21d293 4022d313 522023 22383 120163 200413 100413 6d83a4b7 6d83a517 366f
  //   c00513 c00513 100513 60667
endmodule

module AND (
  input  [31:0] in_1,
  input  [31:0] in_2,
  output [31:0] out_3
);

  assign out_3 = in_1 & in_2;  // AND_Gate and_1, 32 bits wide
endmodule

module OR (
  input  [31:0] in_1,
  input  [31:0] in_2,
  output [31:0] out_3
);

  assign out_3 = in_1 | in_2;  // OR_Gate or_1, 32 bits wide
endmodule

module XOR (
  input  [31:0] in_1,
  input  [31:0] in_2,
  output [31:0] out_3
);

  assign out_3 = in_1 ^ in_2;  // XOR_Gate xor_1, 32 bits wide
endmodule

module SLT (
  input  [31:0] in_1,
  input  [31:0] in_2,
  output [31:0] out_3
);

  wire [30:0] sub_1_out_3;

  SUB sub_1 (.in_1(in_1), .in_2(in_2), .out_3({out_3[0], sub_1_out_3}));

  assign out_3[31:1] = {31{1'b0}};
endmodule

module SLTU (
  input  [31:0] in_1,
  input  [31:0] in_2,
  output [31:0] \unsigned 
);

  wire comparator_1_lt;

  Comparator #(.width(32), .mode("unsigned")) comparator_1 (.a(in_1), .b(in_2), .lt(comparator_1_lt));  // open: gt, eq
  assign \unsigned  = {{31{1'b0}}, comparator_1_lt};  // Bit_Extender bit_extender_1
endmodule

module SLL (
  input  [31:0] in_1,
  input  [31:0] in_2,
  output [31:0] out_3
);

  Shifter #(.width(32)) shifter_1 (.in(in_1), .\dist (in_2[4:0]), .out(out_3));
endmodule

module SRA (
  input  [31:0] in_1,
  input  [31:0] in_2,
  output [31:0] out_3
);

  Shifter #(.width(32), .shift("lr")) shifter_1 (.in(in_1), .\dist (in_2[4:0]), .out(out_3));
endmodule

module SRL (
  input  [31:0] in_1,
  input  [31:0] in_2,
  output [31:0] out_3
);

  Shifter #(.width(32), .shift("lr")) shifter_1 (.in(in_1), .\dist (in_2[4:0]), .out(out_3));
endmodule

module ADD (
  input  [31:0] in_1,
  input  [31:0] in_2,
  output [31:0] out_3
);

  wire and_1_out, and_2_out, and_3_out, and_4_out, and_5_out, and_6_out, and_7_out, and_8_out, and_9_out,
       and_10_out, and_11_out, and_12_out, and_13_out, and_14_out, and_15_out, and_16_out, and_17_out,
       and_18_out, and_19_out, and_20_out, and_21_out, and_22_out, and_23_out, and_24_out, and_25_out,
       and_26_out, and_27_out, and_28_out, and_29_out, and_30_out, and_31_out, and_32_out, and_33_out,
       and_34_out, and_35_out, and_36_out, and_37_out, and_38_out, and_39_out, and_40_out, and_41_out,
       and_42_out, and_43_out, and_44_out, and_45_out, and_46_out, and_47_out, and_48_out, and_49_out,
       and_50_out, and_51_out, and_52_out, and_53_out, and_54_out, and_55_out, and_56_out, and_57_out,
       and_58_out, and_59_out, and_60_out, and_61_out, and_62_out, and_63_out, and_64_out, Cout_out,
       or_1_out, or_2_out, or_3_out, or_4_out, or_5_out, or_6_out, or_7_out, or_8_out, or_9_out, or_10_out,
       or_11_out, or_12_out, or_13_out, or_14_out, or_15_out, or_16_out, or_17_out, or_18_out, or_19_out,
       or_20_out, or_21_out, or_22_out, or_23_out, or_24_out, or_25_out, or_26_out, or_27_out, or_28_out,
       or_29_out, or_30_out, or_31_out, Over_out, xor_1_out, xor_3_out, xor_6_out, xor_8_out, xor_10_out,
       xor_11_out, xor_13_out, xor_15_out, xor_17_out, xor_19_out, xor_21_out, xor_23_out, xor_25_out,
       xor_27_out, xor_30_out, xor_32_out, xor_34_out, xor_35_out, xor_37_out, xor_39_out, xor_41_out,
       xor_43_out, xor_45_out, xor_47_out, xor_49_out, xor_51_out, xor_55_out, xor_57_out, xor_58_out,
       xor_59_out, xor_61_out, xor_63_out;

  and and_1 (and_1_out, in_1[20], in_2[20]);
  and and_2 (and_2_out, or_3_out, xor_1_out);
  or or_1 (or_1_out, and_1_out, and_2_out);
  and and_3 (and_3_out, in_1[31], in_2[31]);
  or Cout (Cout_out, and_3_out, and_4_out);
  xor xor_1 (xor_1_out, in_1[20], in_2[20]);
  xor xor_2 (out_3[20], or_3_out, xor_1_out);
  xor xor_3 (xor_3_out, in_1[31], in_2[31]);
  and and_4 (and_4_out, or_4_out, xor_3_out);
  xor xor_4 (out_3[31], or_4_out, xor_3_out);
  xor Over (Over_out, Cout_out, or_4_out);
  and and_5 (and_5_out, in_1[9], in_2[9]);
  and and_6 (and_6_out, or_5_out, xor_10_out);
  xor xor_5 (out_3[9], or_5_out, xor_10_out);
  or or_2 (or_2_out, and_5_out, and_6_out);
  xor xor_6 (xor_6_out, in_1[19], in_2[19]);
  and and_7 (and_7_out, in_1[19], in_2[19]);
  and and_8 (and_8_out, or_6_out, xor_6_out);
  xor xor_7 (out_3[19], or_6_out, xor_6_out);
  or or_3 (or_3_out, and_7_out, and_8_out);
  xor xor_8 (xor_8_out, in_1[30], in_2[30]);
  and and_9 (and_9_out, in_1[30], in_2[30]);
  and and_10 (and_10_out, or_7_out, xor_8_out);
  xor xor_9 (out_3[30], or_7_out, xor_8_out);
  or or_4 (or_4_out, and_9_out, and_10_out);
  and and_11 (and_11_out, in_1[8], in_2[8]);
  xor xor_10 (xor_10_out, in_1[9], in_2[9]);
  and and_12 (and_12_out, or_8_out, xor_11_out);
  or or_5 (or_5_out, and_11_out, and_12_out);
  and and_13 (and_13_out, in_1[18], in_2[18]);
  and and_14 (and_14_out, or_9_out, xor_13_out);
  or or_6 (or_6_out, and_13_out, and_14_out);
  and and_15 (and_15_out, in_1[29], in_2[29]);
  and and_16 (and_16_out, or_10_out, xor_15_out);
  or or_7 (or_7_out, and_15_out, and_16_out);
  and and_17 (and_17_out, in_1[7], in_2[7]);
  xor xor_11 (xor_11_out, in_1[8], in_2[8]);
  and and_18 (and_18_out, or_13_out, xor_17_out);
  xor xor_12 (out_3[8], or_8_out, xor_11_out);
  or or_8 (or_8_out, and_17_out, and_18_out);
  xor xor_13 (xor_13_out, in_1[18], in_2[18]);
  and and_19 (and_19_out, in_1[17], in_2[17]);
  and and_20 (and_20_out, or_11_out, xor_19_out);
  xor xor_14 (out_3[18], or_9_out, xor_13_out);
  or or_9 (or_9_out, and_19_out, and_20_out);
  xor xor_15 (xor_15_out, in_1[29], in_2[29]);
  and and_21 (and_21_out, in_1[28], in_2[28]);
  and and_22 (and_22_out, or_12_out, xor_21_out);
  xor xor_16 (out_3[29], or_10_out, xor_15_out);
  or or_10 (or_10_out, and_21_out, and_22_out);
  xor xor_17 (xor_17_out, in_1[7], in_2[7]);
  xor xor_18 (out_3[7], or_13_out, xor_17_out);
  xor xor_19 (xor_19_out, in_1[17], in_2[17]);
  and and_23 (and_23_out, in_1[16], in_2[16]);
  xor xor_20 (out_3[17], or_11_out, xor_19_out);
  or or_11 (or_11_out, and_23_out, and_27_out);
  xor xor_21 (xor_21_out, in_1[28], in_2[28]);
  and and_24 (and_24_out, in_1[27], in_2[27]);
  xor xor_22 (out_3[28], or_12_out, xor_21_out);
  or or_12 (or_12_out, and_24_out, and_28_out);
  xor xor_23 (xor_23_out, in_1[6], in_2[6]);
  and and_25 (and_25_out, in_1[6], in_2[6]);
  and and_26 (and_26_out, or_14_out, xor_23_out);
  xor xor_24 (out_3[6], or_14_out, xor_23_out);
  or or_13 (or_13_out, and_25_out, and_26_out);
  xor xor_25 (xor_25_out, in_1[16], in_2[16]);
  and and_27 (and_27_out, or_15_out, xor_25_out);
  xor xor_26 (out_3[16], or_15_out, xor_25_out);
  xor xor_27 (xor_27_out, in_1[27], in_2[27]);
  and and_28 (and_28_out, or_16_out, xor_27_out);
  xor xor_28 (out_3[27], or_16_out, xor_27_out);
  and and_29 (and_29_out, in_1[5], in_2[5]);
  and and_30 (and_30_out, or_17_out, xor_34_out);
  xor xor_29 (out_3[5], or_17_out, xor_34_out);
  or or_14 (or_14_out, and_29_out, and_30_out);
  and and_31 (and_31_out, in_1[15], in_2[15]);
  xor xor_30 (xor_30_out, in_1[15], in_2[15]);
  and and_32 (and_32_out, or_18_out, xor_30_out);
  xor xor_31 (out_3[15], or_18_out, xor_30_out);
  or or_15 (or_15_out, and_31_out, and_32_out);
  xor xor_32 (xor_32_out, in_1[26], in_2[26]);
  and and_33 (and_33_out, in_1[26], in_2[26]);
  and and_34 (and_34_out, or_19_out, xor_32_out);
  xor xor_33 (out_3[26], or_19_out, xor_32_out);
  or or_16 (or_16_out, and_33_out, and_34_out);
  xor xor_34 (xor_34_out, in_1[5], in_2[5]);
  and and_35 (and_35_out, in_1[4], in_2[4]);
  and and_36 (and_36_out, or_20_out, xor_35_out);
  or or_17 (or_17_out, and_35_out, and_36_out);
  and and_37 (and_37_out, in_1[14], in_2[14]);
  and and_38 (and_38_out, or_21_out, xor_37_out);
  or or_18 (or_18_out, and_37_out, and_38_out);
  and and_39 (and_39_out, in_1[25], in_2[25]);
  and and_40 (and_40_out, or_22_out, xor_39_out);
  or or_19 (or_19_out, and_39_out, and_40_out);
  and and_41 (and_41_out, in_1[3], in_2[3]);
  xor xor_35 (xor_35_out, in_1[4], in_2[4]);
  xor xor_36 (out_3[4], or_20_out, xor_35_out);
  or or_20 (or_20_out, and_41_out, and_46_out);
  xor xor_37 (xor_37_out, in_1[14], in_2[14]);
  and and_42 (and_42_out, in_1[13], in_2[13]);
  and and_43 (and_43_out, or_24_out, xor_43_out);
  xor xor_38 (out_3[14], or_21_out, xor_37_out);
  or or_21 (or_21_out, and_42_out, and_43_out);
  xor xor_39 (xor_39_out, in_1[25], in_2[25]);
  and and_44 (and_44_out, in_1[24], in_2[24]);
  and and_45 (and_45_out, or_25_out, xor_45_out);
  xor xor_40 (out_3[25], or_22_out, xor_39_out);
  or or_22 (or_22_out, and_44_out, and_45_out);
  xor xor_41 (xor_41_out, in_1[3], in_2[3]);
  and and_46 (and_46_out, or_23_out, xor_41_out);
  xor xor_42 (out_3[3], or_23_out, xor_41_out);
  xor xor_43 (xor_43_out, in_1[13], in_2[13]);
  xor xor_44 (out_3[13], or_24_out, xor_43_out);
  xor xor_45 (xor_45_out, in_1[24], in_2[24]);
  xor xor_46 (out_3[24], or_25_out, xor_45_out);
  xor xor_47 (xor_47_out, in_1[2], in_2[2]);
  and and_47 (and_47_out, in_1[2], in_2[2]);
  and and_48 (and_48_out, or_26_out, xor_47_out);
  xor xor_48 (out_3[2], or_26_out, xor_47_out);
  or or_23 (or_23_out, and_47_out, and_48_out);
  xor xor_49 (xor_49_out, in_1[12], in_2[12]);
  and and_49 (and_49_out, in_1[12], in_2[12]);
  and and_50 (and_50_out, or_27_out, xor_49_out);
  xor xor_50 (out_3[12], or_27_out, xor_49_out);
  or or_24 (or_24_out, and_49_out, and_50_out);
  xor xor_51 (xor_51_out, in_1[23], in_2[23]);
  and and_51 (and_51_out, in_1[23], in_2[23]);
  and and_52 (and_52_out, or_28_out, xor_51_out);
  xor xor_52 (out_3[23], or_28_out, xor_51_out);
  or or_25 (or_25_out, and_51_out, and_52_out);
  and and_53 (and_53_out, in_1[1], in_2[1]);
  and and_54 (and_54_out, or_29_out, xor_55_out);
  or or_26 (or_26_out, and_53_out, and_54_out);
  and and_55 (and_55_out, in_1[11], in_2[11]);
  and and_56 (and_56_out, or_30_out, xor_57_out);
  xor xor_53 (out_3[11], or_30_out, xor_57_out);
  or or_27 (or_27_out, and_55_out, and_56_out);
  and and_57 (and_57_out, in_1[22], in_2[22]);
  and and_58 (and_58_out, or_31_out, xor_58_out);
  xor xor_54 (out_3[22], or_31_out, xor_58_out);
  or or_28 (or_28_out, and_57_out, and_58_out);
  xor xor_55 (xor_55_out, in_1[1], in_2[1]);
  and and_59 (and_59_out, in_1[0], in_2[0]);
  and and_60 (and_60_out, 1'b0, xor_59_out);
  xor xor_56 (out_3[1], or_29_out, xor_55_out);
  or or_29 (or_29_out, and_59_out, and_60_out);
  and and_61 (and_61_out, in_1[10], in_2[10]);
  xor xor_57 (xor_57_out, in_1[11], in_2[11]);
  and and_62 (and_62_out, or_2_out, xor_61_out);
  or or_30 (or_30_out, and_61_out, and_62_out);
  and and_63 (and_63_out, in_1[21], in_2[21]);
  xor xor_58 (xor_58_out, in_1[22], in_2[22]);
  and and_64 (and_64_out, or_1_out, xor_63_out);
  or or_31 (or_31_out, and_63_out, and_64_out);
  xor xor_59 (xor_59_out, in_1[0], in_2[0]);
  xor xor_60 (out_3[0], 1'b0, xor_59_out);
  xor xor_61 (xor_61_out, in_1[10], in_2[10]);
  xor xor_62 (out_3[10], or_2_out, xor_61_out);
  xor xor_63 (xor_63_out, in_1[21], in_2[21]);
  xor xor_64 (out_3[21], or_1_out, xor_63_out);

  // Other names for the same wires on the sheet: B0 = in_1[0]; B1 = in_1[1]; B2 = in_1[2]; B3 = in_1[3]; B4 = in_1[4];
  //   B5 = in_1[5]; B6 = in_1[6]; B7 = in_1[7]; B8 = in_1[8]; B9 = in_1[9]; B10 = in_1[10]; B11 = in_1[11];
  //   B12 = in_1[12]; B13 = in_1[13]; B14 = in_1[14]; B15 = in_1[15]; B16 = in_1[16]; B17 = in_1[17]; B18 = in_1[18];
  //   B19 = in_1[19]; B20 = in_1[20]; B21 = in_1[21]; B22 = in_1[22]; B23 = in_1[23]; B24 = in_1[24]; B25 = in_1[25];
  //   B26 = in_1[26]; B27 = in_1[27]; B28 = in_1[28]; B29 = in_1[29]; B30 = in_1[30]; B31 = in_1[31]; A0 = in_2[0];
  //   A1 = in_2[1]; A2 = in_2[2]; A3 = in_2[3]; A4 = in_2[4]; A5 = in_2[5]; A6 = in_2[6]; A7 = in_2[7]; A8 = in_2[8];
  //   A9 = in_2[9]; A10 = in_2[10]; A11 = in_2[11]; A12 = in_2[12]; A13 = in_2[13]; A14 = in_2[14]; A15 = in_2[15];
  //   A16 = in_2[16]; A17 = in_2[17]; A18 = in_2[18]; A19 = in_2[19]; A20 = in_2[20]; A21 = in_2[21]; A22 = in_2[22];
  //   A23 = in_2[23]; A24 = in_2[24]; A25 = in_2[25]; A26 = in_2[26]; A27 = in_2[27]; A28 = in_2[28]; A29 = in_2[29];
  //   A30 = in_2[30]; A31 = in_2[31]; S0 = out_3[0]; S1 = out_3[1]; S2 = out_3[2]; S3 = out_3[3]; S4 = out_3[4];
  //   S5 = out_3[5]; S6 = out_3[6]; S7 = out_3[7]; S8 = out_3[8]; S9 = out_3[9]; S10 = out_3[10]; S11 = out_3[11];
  //   S12 = out_3[12]; S13 = out_3[13]; S14 = out_3[14]; S15 = out_3[15]; S16 = out_3[16]; S17 = out_3[17];
  //   S18 = out_3[18]; S19 = out_3[19]; S20 = out_3[20]; S21 = out_3[21]; S22 = out_3[22]; S23 = out_3[23];
  //   S24 = out_3[24]; S25 = out_3[25]; S26 = out_3[26]; S27 = out_3[27]; S28 = out_3[28]; S29 = out_3[29];
  //   S30 = out_3[30]; S31 = out_3[31]
endmodule

module SUB (
  input  [31:0] in_1,
  input  [31:0] in_2,
  output [31:0] out_3
);

  wire and_1_out, and_2_out, and_3_out, and_4_out, and_5_out, and_6_out, and_7_out, and_8_out, and_9_out,
       and_10_out, and_11_out, and_12_out, and_13_out, and_14_out, and_15_out, and_16_out, and_17_out,
       and_18_out, and_19_out, and_20_out, and_21_out, and_22_out, and_23_out, and_24_out, and_25_out,
       and_26_out, and_27_out, and_28_out, and_29_out, and_30_out, and_31_out, and_32_out, and_33_out,
       and_34_out, and_35_out, and_36_out, and_37_out, and_38_out, and_39_out, and_40_out, and_41_out,
       and_42_out, and_43_out, and_44_out, and_45_out, and_46_out, and_47_out, and_48_out, and_49_out,
       and_50_out, and_51_out, and_52_out, and_53_out, and_54_out, and_55_out, and_56_out, and_57_out,
       and_58_out, and_59_out, and_60_out, and_61_out, and_62_out, and_63_out, and_64_out, Bout_out,
       not_1_out, not_2_out, not_3_out, not_4_out, not_5_out, not_6_out, not_7_out, not_8_out, not_9_out,
       not_10_out, not_11_out, not_12_out, not_13_out, not_14_out, not_15_out, not_16_out, not_17_out,
       not_18_out, not_19_out, not_20_out, not_21_out, not_22_out, not_23_out, not_24_out, not_25_out,
       not_26_out, not_27_out, not_28_out, not_29_out, not_30_out, not_31_out, not_32_out, not_33_out,
       not_34_out, not_35_out, not_36_out, not_37_out, not_38_out, not_39_out, not_40_out, not_41_out,
       not_42_out, not_43_out, not_44_out, not_45_out, not_46_out, not_47_out, not_48_out, not_49_out,
       not_50_out, not_51_out, not_52_out, not_53_out, not_54_out, not_55_out, not_56_out, not_57_out,
       not_58_out, not_59_out, not_60_out, not_61_out, not_62_out, not_63_out, not_64_out, or_1_out,
       or_2_out, or_3_out, or_4_out, or_5_out, or_6_out, or_7_out, or_8_out, or_9_out, or_10_out, or_11_out,
       or_12_out, or_13_out, or_14_out, or_15_out, or_16_out, or_17_out, or_18_out, or_19_out, or_20_out,
       or_21_out, or_22_out, or_23_out, or_24_out, or_25_out, or_26_out, or_27_out, or_28_out, or_29_out,
       or_30_out, or_31_out, Over_out, xor_1_out, xor_3_out, xor_6_out, xor_8_out, xor_10_out, xor_12_out,
       xor_14_out, xor_16_out, xor_17_out, xor_19_out, xor_21_out, xor_23_out, xor_25_out, xor_27_out,
       xor_30_out, xor_32_out, xor_34_out, xor_35_out, xor_37_out, xor_39_out, xor_41_out, xor_43_out,
       xor_45_out, xor_47_out, xor_49_out, xor_51_out, xor_54_out, xor_56_out, xor_58_out, xor_59_out,
       xor_61_out, xor_63_out;

  not not_1 (not_1_out, in_2[20]);
  and and_1 (and_1_out, in_1[20], not_1_out);
  and and_2 (and_2_out, or_3_out, not_3_out);
  or or_1 (or_1_out, and_1_out, and_2_out);
  not not_2 (not_2_out, in_2[30]);
  and and_3 (and_3_out, in_1[30], not_2_out);
  and and_4 (and_4_out, or_4_out, not_4_out);
  or Bout (Bout_out, and_3_out, and_4_out);
  xor xor_1 (xor_1_out, in_1[20], in_2[20]);
  not not_3 (not_3_out, xor_1_out);
  xor xor_2 (out_3[20], or_3_out, xor_1_out);
  xor xor_3 (xor_3_out, in_1[30], in_2[30]);
  not not_4 (not_4_out, xor_3_out);
  xor xor_4 (out_3[31], or_4_out, xor_3_out);
  xor Over (Over_out, Bout_out, or_4_out);
  not not_5 (not_5_out, in_2[9]);
  and and_5 (and_5_out, in_1[9], not_5_out);
  not not_6 (not_6_out, xor_10_out);
  and and_6 (and_6_out, or_5_out, not_6_out);
  xor xor_5 (out_3[9], or_5_out, xor_10_out);
  or or_2 (or_2_out, and_5_out, and_6_out);
  not not_7 (not_7_out, in_2[19]);
  and and_7 (and_7_out, in_1[19], not_7_out);
  xor xor_6 (xor_6_out, in_1[19], in_2[19]);
  not not_8 (not_8_out, xor_6_out);
  and and_8 (and_8_out, or_6_out, not_8_out);
  xor xor_7 (out_3[19], or_6_out, xor_6_out);
  or or_3 (or_3_out, and_7_out, and_8_out);
  not not_9 (not_9_out, in_2[30]);
  xor xor_8 (xor_8_out, in_1[30], in_2[30]);
  and and_9 (and_9_out, in_1[30], not_9_out);
  not not_10 (not_10_out, xor_8_out);
  and and_10 (and_10_out, or_7_out, not_10_out);
  xor xor_9 (out_3[30], or_7_out, xor_8_out);
  or or_4 (or_4_out, and_9_out, and_10_out);
  not not_11 (not_11_out, in_2[8]);
  and and_11 (and_11_out, in_1[8], not_11_out);
  xor xor_10 (xor_10_out, in_1[9], in_2[9]);
  not not_12 (not_12_out, xor_12_out);
  and and_12 (and_12_out, or_8_out, not_12_out);
  or or_5 (or_5_out, and_11_out, and_12_out);
  not not_13 (not_13_out, in_2[18]);
  and and_13 (and_13_out, in_1[18], not_13_out);
  not not_14 (not_14_out, xor_14_out);
  and and_14 (and_14_out, or_9_out, not_14_out);
  or or_6 (or_6_out, and_13_out, and_14_out);
  not not_15 (not_15_out, in_2[29]);
  and and_15 (and_15_out, in_1[29], not_15_out);
  not not_16 (not_16_out, xor_16_out);
  and and_16 (and_16_out, or_10_out, not_16_out);
  xor xor_11 (out_3[29], or_10_out, xor_16_out);
  or or_7 (or_7_out, and_15_out, and_16_out);
  not not_17 (not_17_out, in_2[7]);
  xor xor_12 (xor_12_out, in_1[8], in_2[8]);
  and and_17 (and_17_out, in_1[7], not_17_out);
  and and_18 (and_18_out, or_13_out, not_22_out);
  xor xor_13 (out_3[8], or_8_out, xor_12_out);
  or or_8 (or_8_out, and_17_out, and_18_out);
  not not_18 (not_18_out, in_2[17]);
  xor xor_14 (xor_14_out, in_1[18], in_2[18]);
  and and_19 (and_19_out, in_1[17], not_18_out);
  not not_19 (not_19_out, xor_19_out);
  and and_20 (and_20_out, or_11_out, not_19_out);
  xor xor_15 (out_3[18], or_9_out, xor_14_out);
  or or_9 (or_9_out, and_19_out, and_20_out);
  not not_20 (not_20_out, in_2[28]);
  xor xor_16 (xor_16_out, in_1[29], in_2[29]);
  and and_21 (and_21_out, in_1[28], not_20_out);
  not not_21 (not_21_out, xor_21_out);
  and and_22 (and_22_out, or_12_out, not_21_out);
  or or_10 (or_10_out, and_21_out, and_22_out);
  xor xor_17 (xor_17_out, in_1[7], in_2[7]);
  not not_22 (not_22_out, xor_17_out);
  xor xor_18 (out_3[7], or_13_out, xor_17_out);
  xor xor_19 (xor_19_out, in_1[17], in_2[17]);
  and and_23 (and_23_out, in_1[16], not_26_out);
  xor xor_20 (out_3[17], or_11_out, xor_19_out);
  or or_11 (or_11_out, and_23_out, and_28_out);
  not not_23 (not_23_out, in_2[27]);
  and and_24 (and_24_out, in_1[27], not_23_out);
  xor xor_21 (xor_21_out, in_1[28], in_2[28]);
  and and_25 (and_25_out, or_16_out, not_28_out);
  xor xor_22 (out_3[28], or_12_out, xor_21_out);
  or or_12 (or_12_out, and_24_out, and_25_out);
  not not_24 (not_24_out, in_2[6]);
  and and_26 (and_26_out, in_1[6], not_24_out);
  xor xor_23 (xor_23_out, in_1[6], in_2[6]);
  not not_25 (not_25_out, xor_23_out);
  and and_27 (and_27_out, or_14_out, not_25_out);
  xor xor_24 (out_3[6], or_14_out, xor_23_out);
  or or_13 (or_13_out, and_26_out, and_27_out);
  not not_26 (not_26_out, in_2[16]);
  xor xor_25 (xor_25_out, in_1[16], in_2[16]);
  not not_27 (not_27_out, xor_25_out);
  and and_28 (and_28_out, or_15_out, not_27_out);
  xor xor_26 (out_3[16], or_15_out, xor_25_out);
  xor xor_27 (xor_27_out, in_1[27], in_2[27]);
  not not_28 (not_28_out, xor_27_out);
  xor xor_28 (out_3[27], or_16_out, xor_27_out);
  not not_29 (not_29_out, in_2[5]);
  and and_29 (and_29_out, in_1[5], not_29_out);
  not not_30 (not_30_out, xor_34_out);
  and and_30 (and_30_out, or_17_out, not_30_out);
  xor xor_29 (out_3[5], or_17_out, xor_34_out);
  or or_14 (or_14_out, and_29_out, and_30_out);
  not not_31 (not_31_out, in_2[15]);
  and and_31 (and_31_out, in_1[15], not_31_out);
  xor xor_30 (xor_30_out, in_1[15], in_2[15]);
  not not_32 (not_32_out, xor_30_out);
  and and_32 (and_32_out, or_18_out, not_32_out);
  xor xor_31 (out_3[15], or_18_out, xor_30_out);
  or or_15 (or_15_out, and_31_out, and_32_out);
  not not_33 (not_33_out, in_2[26]);
  and and_33 (and_33_out, in_1[26], not_33_out);
  xor xor_32 (xor_32_out, in_1[26], in_2[26]);
  not not_34 (not_34_out, xor_32_out);
  and and_34 (and_34_out, or_19_out, not_34_out);
  xor xor_33 (out_3[26], or_19_out, xor_32_out);
  or or_16 (or_16_out, and_33_out, and_34_out);
  not not_35 (not_35_out, in_2[4]);
  xor xor_34 (xor_34_out, in_1[5], in_2[5]);
  and and_35 (and_35_out, in_1[4], not_35_out);
  not not_36 (not_36_out, xor_35_out);
  and and_36 (and_36_out, or_20_out, not_36_out);
  or or_17 (or_17_out, and_35_out, and_36_out);
  not not_37 (not_37_out, in_2[14]);
  and and_37 (and_37_out, in_1[14], not_37_out);
  not not_38 (not_38_out, xor_37_out);
  and and_38 (and_38_out, or_21_out, not_38_out);
  or or_18 (or_18_out, and_37_out, and_38_out);
  not not_39 (not_39_out, in_2[25]);
  and and_39 (and_39_out, in_1[25], not_39_out);
  not not_40 (not_40_out, xor_39_out);
  and and_40 (and_40_out, or_22_out, not_40_out);
  or or_19 (or_19_out, and_39_out, and_40_out);
  and and_41 (and_41_out, in_1[3], not_44_out);
  xor xor_35 (xor_35_out, in_1[4], in_2[4]);
  xor xor_36 (out_3[4], or_20_out, xor_35_out);
  or or_20 (or_20_out, and_41_out, and_46_out);
  not not_41 (not_41_out, in_2[13]);
  and and_42 (and_42_out, in_1[13], not_41_out);
  xor xor_37 (xor_37_out, in_1[14], in_2[14]);
  and and_43 (and_43_out, or_25_out, not_46_out);
  xor xor_38 (out_3[14], or_21_out, xor_37_out);
  or or_21 (or_21_out, and_42_out, and_43_out);
  not not_42 (not_42_out, in_2[24]);
  and and_44 (and_44_out, in_1[24], not_42_out);
  xor xor_39 (xor_39_out, in_1[25], in_2[25]);
  not not_43 (not_43_out, xor_45_out);
  and and_45 (and_45_out, or_23_out, not_43_out);
  xor xor_40 (out_3[25], or_22_out, xor_39_out);
  or or_22 (or_22_out, and_44_out, and_45_out);
  not not_44 (not_44_out, in_2[3]);
  xor xor_41 (xor_41_out, in_1[3], in_2[3]);
  not not_45 (not_45_out, xor_41_out);
  and and_46 (and_46_out, or_24_out, not_45_out);
  xor xor_42 (out_3[3], or_24_out, xor_41_out);
  xor xor_43 (xor_43_out, in_1[13], in_2[13]);
  not not_46 (not_46_out, xor_43_out);
  xor xor_44 (out_3[13], or_25_out, xor_43_out);
  and and_47 (and_47_out, in_1[23], not_51_out);
  xor xor_45 (xor_45_out, in_1[24], in_2[24]);
  xor xor_46 (out_3[24], or_23_out, xor_45_out);
  or or_23 (or_23_out, and_47_out, and_52_out);
  not not_47 (not_47_out, in_2[2]);
  and and_48 (and_48_out, in_1[2], not_47_out);
  xor xor_47 (xor_47_out, in_1[2], in_2[2]);
  not not_48 (not_48_out, xor_47_out);
  and and_49 (and_49_out, or_26_out, not_48_out);
  xor xor_48 (out_3[2], or_26_out, xor_47_out);
  or or_24 (or_24_out, and_48_out, and_49_out);
  not not_49 (not_49_out, in_2[12]);
  xor xor_49 (xor_49_out, in_1[12], in_2[12]);
  and and_50 (and_50_out, in_1[12], not_49_out);
  not not_50 (not_50_out, xor_49_out);
  and and_51 (and_51_out, or_27_out, not_50_out);
  xor xor_50 (out_3[12], or_27_out, xor_49_out);
  or or_25 (or_25_out, and_50_out, and_51_out);
  not not_51 (not_51_out, in_2[23]);
  xor xor_51 (xor_51_out, in_1[23], in_2[23]);
  not not_52 (not_52_out, xor_51_out);
  and and_52 (and_52_out, or_28_out, not_52_out);
  xor xor_52 (out_3[23], or_28_out, xor_51_out);
  not not_53 (not_53_out, in_2[1]);
  and and_53 (and_53_out, in_1[1], not_53_out);
  not not_54 (not_54_out, xor_56_out);
  and and_54 (and_54_out, or_29_out, not_54_out);
  or or_26 (or_26_out, and_53_out, and_54_out);
  not not_55 (not_55_out, in_2[11]);
  and and_55 (and_55_out, in_1[11], not_55_out);
  not not_56 (not_56_out, xor_58_out);
  and and_56 (and_56_out, or_30_out, not_56_out);
  xor xor_53 (out_3[11], or_30_out, xor_58_out);
  or or_27 (or_27_out, and_55_out, and_56_out);
  not not_57 (not_57_out, in_2[22]);
  xor xor_54 (xor_54_out, in_1[22], in_2[22]);
  and and_57 (and_57_out, in_1[22], not_57_out);
  not not_58 (not_58_out, xor_54_out);
  and and_58 (and_58_out, or_31_out, not_58_out);
  xor xor_55 (out_3[22], or_31_out, xor_54_out);
  or or_28 (or_28_out, and_57_out, and_58_out);
  not not_59 (not_59_out, in_2[0]);
  and and_59 (and_59_out, in_1[0], not_59_out);
  xor xor_56 (xor_56_out, in_1[1], in_2[1]);
  not not_60 (not_60_out, xor_59_out);
  and and_60 (and_60_out, 1'b0, not_60_out);
  xor xor_57 (out_3[1], or_29_out, xor_56_out);
  or or_29 (or_29_out, and_59_out, and_60_out);
  not not_61 (not_61_out, in_2[10]);
  xor xor_58 (xor_58_out, in_1[11], in_2[11]);
  and and_61 (and_61_out, in_1[10], not_61_out);
  not not_62 (not_62_out, xor_61_out);
  and and_62 (and_62_out, or_2_out, not_62_out);
  or or_30 (or_30_out, and_61_out, and_62_out);
  not not_63 (not_63_out, in_2[21]);
  and and_63 (and_63_out, in_1[21], not_63_out);
  not not_64 (not_64_out, xor_63_out);
  and and_64 (and_64_out, or_1_out, not_64_out);
  or or_31 (or_31_out, and_63_out, and_64_out);
  xor xor_59 (xor_59_out, in_1[0], in_2[0]);
  xor xor_60 (out_3[0], 1'b0, xor_59_out);
  xor xor_61 (xor_61_out, in_1[10], in_2[10]);
  xor xor_62 (out_3[10], or_2_out, xor_61_out);
  xor xor_63 (xor_63_out, in_1[21], in_2[21]);
  xor xor_64 (out_3[21], or_1_out, xor_63_out);

  // Other names for the same wires on the sheet: B0 = in_1[0]; B1 = in_1[1]; B2 = in_1[2]; B3 = in_1[3]; B4 = in_1[4];
  //   B5 = in_1[5]; B6 = in_1[6]; B7 = in_1[7]; B8 = in_1[8]; B9 = in_1[9]; B10 = in_1[10]; B11 = in_1[11];
  //   B12 = in_1[12]; B13 = in_1[13]; B14 = in_1[14]; B15 = in_1[15]; B16 = in_1[16]; B17 = in_1[17]; B18 = in_1[18];
  //   B19 = in_1[19]; B20 = in_1[20]; B21 = in_1[21]; B22 = in_1[22]; B23 = in_1[23]; B24 = in_1[24]; B25 = in_1[25];
  //   B26 = in_1[26]; B27 = in_1[27]; B28 = in_1[28]; B29 = in_1[29]; B30 = in_1[30]; B31 = in_1[31]; A0 = in_2[0];
  //   A1 = in_2[1]; A2 = in_2[2]; A3 = in_2[3]; A4 = in_2[4]; A5 = in_2[5]; A6 = in_2[6]; A7 = in_2[7]; A8 = in_2[8];
  //   A9 = in_2[9]; A10 = in_2[10]; A11 = in_2[11]; A12 = in_2[12]; A13 = in_2[13]; A14 = in_2[14]; A15 = in_2[15];
  //   A16 = in_2[16]; A17 = in_2[17]; A18 = in_2[18]; A19 = in_2[19]; A20 = in_2[20]; A21 = in_2[21]; A22 = in_2[22];
  //   A23 = in_2[23]; A24 = in_2[24]; A25 = in_2[25]; A26 = in_2[26]; A27 = in_2[27]; A28 = in_2[28]; A29 = in_2[29];
  //   A30 = in_2[30]; A31 = in_2[31]; V0 = out_3[0]; V1 = out_3[1]; V2 = out_3[2]; V3 = out_3[3]; V4 = out_3[4];
  //   V5 = out_3[5]; V6 = out_3[6]; V7 = out_3[7]; V8 = out_3[8]; V9 = out_3[9]; V10 = out_3[10]; V11 = out_3[11];
  //   V12 = out_3[12]; V13 = out_3[13]; V14 = out_3[14]; V15 = out_3[15]; V16 = out_3[16]; V17 = out_3[17];
  //   V18 = out_3[18]; V19 = out_3[19]; V20 = out_3[20]; V21 = out_3[21]; V22 = out_3[22]; V23 = out_3[23];
  //   V24 = out_3[24]; V25 = out_3[25]; V26 = out_3[26]; V27 = out_3[27]; V28 = out_3[28]; V29 = out_3[29];
  //   V30 = out_3[30]; V31 = out_3[31]
endmodule

module PC (
  input  [11:0] in_1,
  input  in_2,
  output [11:0] out_3
);

  Register #(.width(12)) register_1 (.D(in_1), .en(1'b1), .Q(out_3), .clk(in_2));  // open: clr
endmodule

// PC adder
module _4 (
  input  [11:0] in_1,
  input  [11:0] in_2,
  output [11:0] out_3
);

  wire and_1_out, and_2_out, and_3_out, and_4_out, and_5_out, and_6_out, and_7_out, and_8_out, and_9_out,
       and_10_out, and_11_out, and_12_out, and_13_out, and_14_out, and_15_out, and_16_out, and_17_out,
       and_18_out, and_19_out, and_20_out, and_21_out, and_22_out, and_23_out, and_24_out, or_2_out,
       or_3_out, or_4_out, or_5_out, or_6_out, or_7_out, or_8_out, or_9_out, or_10_out, or_11_out, or_12_out,
       xor_1_out, xor_3_out, xor_5_out, xor_7_out, xor_9_out, xor_12_out, xor_13_out, xor_15_out, xor_17_out,
       xor_19_out, xor_21_out, xor_23_out;

  and and_1 (and_1_out, in_2[11], in_1[11]);
  or or_1 (out_3[11], and_1_out, and_2_out);
  xor xor_1 (xor_1_out, in_2[11], in_1[11]);
  and and_2 (and_2_out, or_2_out, xor_1_out);
  // XOR_Gate xor_2 has open pins: in0=or_2_out, in1=xor_1_out, out=open
  xor xor_3 (xor_3_out, in_2[10], in_1[10]);
  and and_3 (and_3_out, in_2[10], in_1[10]);
  and and_4 (and_4_out, or_3_out, xor_3_out);
  xor xor_4 (out_3[10], or_3_out, xor_3_out);
  or or_2 (or_2_out, and_3_out, and_4_out);
  and and_5 (and_5_out, in_2[9], in_1[9]);
  and and_6 (and_6_out, or_4_out, xor_5_out);
  or or_3 (or_3_out, and_5_out, and_6_out);
  xor xor_5 (xor_5_out, in_2[9], in_1[9]);
  and and_7 (and_7_out, in_2[8], in_1[8]);
  and and_8 (and_8_out, or_5_out, xor_7_out);
  xor xor_6 (out_3[9], or_4_out, xor_5_out);
  or or_4 (or_4_out, and_7_out, and_8_out);
  xor xor_7 (xor_7_out, in_2[8], in_1[8]);
  xor xor_8 (out_3[8], or_5_out, xor_7_out);
  xor xor_9 (xor_9_out, in_2[7], in_1[7]);
  and and_9 (and_9_out, in_2[7], in_1[7]);
  and and_10 (and_10_out, or_6_out, xor_9_out);
  xor xor_10 (out_3[7], or_6_out, xor_9_out);
  or or_5 (or_5_out, and_9_out, and_10_out);
  and and_11 (and_11_out, in_2[6], in_1[6]);
  and and_12 (and_12_out, or_7_out, xor_12_out);
  xor xor_11 (out_3[6], or_7_out, xor_12_out);
  or or_6 (or_6_out, and_11_out, and_12_out);
  xor xor_12 (xor_12_out, in_2[6], in_1[6]);
  and and_13 (and_13_out, in_2[5], in_1[5]);
  and and_14 (and_14_out, or_8_out, xor_13_out);
  or or_7 (or_7_out, and_13_out, and_14_out);
  xor xor_13 (xor_13_out, in_2[5], in_1[5]);
  and and_15 (and_15_out, in_2[4], in_1[4]);
  xor xor_14 (out_3[5], or_8_out, xor_13_out);
  or or_8 (or_8_out, and_15_out, and_16_out);
  xor xor_15 (xor_15_out, in_2[4], in_1[4]);
  and and_16 (and_16_out, or_9_out, xor_15_out);
  xor xor_16 (out_3[4], or_9_out, xor_15_out);
  and and_17 (and_17_out, in_2[3], in_1[3]);
  xor xor_17 (xor_17_out, in_2[3], in_1[3]);
  and and_18 (and_18_out, or_10_out, xor_17_out);
  xor xor_18 (out_3[3], or_10_out, xor_17_out);
  or or_9 (or_9_out, and_17_out, and_18_out);
  and and_19 (and_19_out, in_2[2], in_1[2]);
  and and_20 (and_20_out, or_11_out, xor_19_out);
  or or_10 (or_10_out, and_19_out, and_20_out);
  and and_21 (and_21_out, in_2[1], in_1[1]);
  xor xor_19 (xor_19_out, in_2[2], in_1[2]);
  and and_22 (and_22_out, or_12_out, xor_21_out);
  xor xor_20 (out_3[2], or_11_out, xor_19_out);
  or or_11 (or_11_out, and_21_out, and_22_out);
  xor xor_21 (xor_21_out, in_2[1], in_1[1]);
  and and_23 (and_23_out, in_2[0], in_1[0]);
  xor xor_22 (out_3[1], or_12_out, xor_21_out);
  or or_12 (or_12_out, and_23_out, and_24_out);
  xor xor_23 (xor_23_out, in_2[0], in_1[0]);
  and and_24 (and_24_out, 1'b0, xor_23_out);
  xor xor_24 (out_3[0], 1'b0, xor_23_out);
endmodule

module ALU (
  input  [31:0] in_1,
  input  [31:0] in_2,
  input  srl___sra,
  input  selectbot_for_add_or_sub,
  input  [2:0] in_5,
  output [31:0] out_6
);

  wire [31:0] add_1_out_3, and_1_out_3, multiplexer_1_out, multiplexer_3_out, or_1_out_3, sll_1_out_3,
       slt_1_out_3, sltu_1_unsigned, sra_1_out_3, srl_1_out_3, sub_1_out_3, xor_1_out_3;

  XOR xor_1 (.in_1(in_1), .in_2(in_2), .out_3(xor_1_out_3));
  OR or_1 (.in_1(in_1), .in_2(in_2), .out_3(or_1_out_3));
  AND and_1 (.in_1(in_1), .in_2(in_2), .out_3(and_1_out_3));
  SLTU sltu_1 (.in_1(in_2), .in_2(in_1), .\unsigned (sltu_1_unsigned));
  SLT slt_1 (.in_1(in_1), .in_2(in_2), .out_3(slt_1_out_3));
  SLL sll_1 (.in_1(in_2), .in_2(in_1), .out_3(sll_1_out_3));
  SRA sra_1 (.in_1(in_2), .in_2(in_1), .out_3(sra_1_out_3));
  Multiplexer #(.width(32), .enable("false")) multiplexer_1 (
    .in0(srl_1_out_3), .in1(sra_1_out_3), .out(multiplexer_1_out), .sel(srl___sra));
  Multiplexer #(.select(3), .width(32), .enable("false")) multiplexer_2 (
    .in0(multiplexer_3_out), .in1(sll_1_out_3), .in2(slt_1_out_3), .in3(sltu_1_unsigned), .in4(xor_1_out_3),
    .in5(multiplexer_1_out), .in6(or_1_out_3), .in7(and_1_out_3), .out(out_6), .sel(in_5));
  SRL srl_1 (.in_1(in_2), .in_2(in_1), .out_3(srl_1_out_3));
  SUB sub_1 (.in_1(in_1), .in_2(in_2), .out_3(sub_1_out_3));
  ADD add_1 (.in_1(in_1), .in_2(in_2), .out_3(add_1_out_3));
  Multiplexer #(.width(32), .enable("false")) multiplexer_3 (
    .in0(add_1_out_3), .in1(sub_1_out_3), .out(multiplexer_3_out), .sel(selectbot_for_add_or_sub));
endmodule

// Reg File
module RegFile (
  input  [31:0] in_1,
  input  in_2,
  input  Reg_En,
  input  [4:0] dest,
  input  [4:0] rs2,
  input  [4:0] rs1,
  output [31:0] out_7,
  output [31:0] out_8
);

  wire E1R0, E1R1, E1R2, E1R3, E1R4, E1R5, E1R6, E1R7, E1R8, E1R9, E1R10, E1R11, E1R12, E1R13, E1R14, E1R15,
       E1R16, E1R17, E1R18, E1R19, E1R20, E1R21, E1R22, E1R23, E1R24, E1R25, E1R26, E1R27, E1R28, E1R29,
       E1R30, E1R31;
  wire [31:0] O1R0, O1R1, O1R2, O1R3, O1R4, O1R5, O1R6, O1R7, O1R8, O1R9, O1R10, O1R11, O1R12, O1R13, O1R14,
       O1R15, O1R16, O1R17, O1R18, O1R19, O1R20, O1R21, O1R22, O1R23, O1R24, O1R25, O1R26, O1R27, O1R28,
       O1R29, O1R30, O1R31;

  Demultiplexer #(.select(5), .enable("false")) demultiplexer_1 (
    .out0(E1R0), .out1(E1R1), .out2(E1R2), .out3(E1R3), .out4(E1R4), .out5(E1R5), .out6(E1R6), .out7(E1R7),
    .out8(E1R8), .out9(E1R9), .out10(E1R10), .out11(E1R11), .out12(E1R12), .out13(E1R13), .out14(E1R14),
    .out15(E1R15), .out16(E1R16), .out17(E1R17), .out18(E1R18), .out19(E1R19), .out20(E1R20), .out21(E1R21),
    .out22(E1R22), .out23(E1R23), .out24(E1R24), .out25(E1R25), .out26(E1R26), .out27(E1R27), .out28(E1R28),
    .out29(E1R29), .out30(E1R30), .out31(E1R31), .in(Reg_En), .sel(dest));
  Register #(.width(32)) register_1 (.D(in_1), .en(1'b0), .Q(O1R0), .clk(in_2), .clr(1'b0));
  Register #(.width(32)) register_2 (.D(in_1), .en(E1R1), .Q(O1R1), .clk(in_2), .clr(1'b0));
  Register #(.width(32)) register_3 (.D(in_1), .en(E1R2), .Q(O1R2), .clk(in_2), .clr(1'b0));
  Register #(.width(32)) register_4 (.D(in_1), .en(E1R3), .Q(O1R3), .clk(in_2), .clr(1'b0));
  Register #(.width(32)) register_5 (.D(in_1), .en(E1R4), .Q(O1R4), .clk(in_2), .clr(1'b0));
  Register #(.width(32)) register_6 (.D(in_1), .en(E1R5), .Q(O1R5), .clk(in_2), .clr(1'b0));
  Register #(.width(32)) register_7 (.D(in_1), .en(E1R6), .Q(O1R6), .clk(in_2), .clr(1'b0));
  Register #(.width(32)) register_8 (.D(in_1), .en(E1R7), .Q(O1R7), .clk(in_2), .clr(1'b0));
  Register #(.width(32)) register_9 (.D(in_1), .en(E1R8), .Q(O1R8), .clk(in_2), .clr(1'b0));
  Register #(.width(32)) register_10 (.D(in_1), .en(E1R9), .Q(O1R9), .clk(in_2), .clr(1'b0));
  Register #(.width(32)) register_11 (.D(in_1), .en(E1R10), .Q(O1R10), .clk(in_2), .clr(1'b0));
  Register #(.width(32)) register_12 (.D(in_1), .en(E1R11), .Q(O1R11), .clk(in_2), .clr(1'b0));
  Register #(.width(32)) register_13 (.D(in_1), .en(E1R12), .Q(O1R12), .clk(in_2), .clr(1'b0));
  Register #(.width(32)) register_14 (.D(in_1), .en(E1R13), .Q(O1R13), .clk(in_2), .clr(1'b0));
  Register #(.width(32)) register_15 (.D(in_1), .en(E1R14), .Q(O1R14), .clk(in_2), .clr(1'b0));
  Register #(.width(32)) register_16 (.D(in_1), .en(E1R15), .Q(O1R15), .clk(in_2), .clr(1'b0));
  Register #(.width(32)) register_17 (.D(in_1), .en(E1R16), .Q(O1R16), .clk(in_2), .clr(1'b0));
  Register #(.width(32)) register_18 (.D(in_1), .en(E1R17), .Q(O1R17), .clk(in_2), .clr(1'b0));
  Register #(.width(32)) register_19 (.D(in_1), .en(E1R18), .Q(O1R18), .clk(in_2), .clr(1'b0));
  Register #(.width(32)) register_20 (.D(in_1), .en(E1R19), .Q(O1R19), .clk(in_2), .clr(1'b0));
  Register #(.width(32)) register_21 (.D(in_1), .en(E1R20), .Q(O1R20), .clk(in_2), .clr(1'b0));
  Register #(.width(32)) register_22 (.D(in_1), .en(E1R21), .Q(O1R21), .clk(in_2), .clr(1'b0));
  Register #(.width(32)) register_23 (.D(in_1), .en(E1R22), .Q(O1R22), .clk(in_2), .clr(1'b0));
  Register #(.width(32)) register_24 (.D(in_1), .en(E1R23), .Q(O1R23), .clk(in_2), .clr(1'b0));
  Register #(.width(32)) register_25 (.D(in_1), .en(E1R24), .Q(O1R24), .clk(in_2), .clr(1'b0));
  Register #(.width(32)) register_26 (.D(in_1), .en(E1R25), .Q(O1R25), .clk(in_2), .clr(1'b0));
  Register #(.width(32)) register_27 (.D(in_1), .en(E1R26), .Q(O1R26), .clk(in_2), .clr(1'b0));
  Register #(.width(32)) register_28 (.D(in_1), .en(E1R27), .Q(O1R27), .clk(in_2), .clr(1'b0));
  Register #(.width(32)) register_29 (.D(in_1), .en(E1R28), .Q(O1R28), .clk(in_2), .clr(1'b0));
  Register #(.width(32)) register_30 (.D(in_1), .en(E1R29), .Q(O1R29), .clk(in_2), .clr(1'b0));
  Register #(.width(32)) register_31 (.D(in_1), .en(E1R30), .Q(O1R30), .clk(in_2), .clr(1'b0));
  Register #(.width(32)) register_32 (.D(in_1), .en(E1R31), .Q(O1R31), .clk(in_2), .clr(1'b0));
  Multiplexer #(.select(5), .width(32), .enable("false")) multiplexer_1 (
    .in0(O1R0), .in1(O1R1), .in2(O1R2), .in3(O1R3), .in4(O1R4), .in5(O1R5), .in6(O1R6), .in7(O1R7),
    .in8(O1R8), .in9(O1R9), .in10(O1R10), .in11(O1R11), .in12(O1R12), .in13(O1R13), .in14(O1R14),
    .in15(O1R15), .in16(O1R16), .in17(O1R17), .in18(O1R18), .in19(O1R19), .in20(O1R20), .in21(O1R21),
    .in22(O1R22), .in23(O1R23), .in24(O1R24), .in25(O1R25), .in26(O1R26), .in27(O1R27), .in28(O1R28),
    .in29(O1R29), .in30(O1R30), .in31(O1R31), .out(out_7), .sel(rs1));
  Multiplexer #(.select(5), .width(32), .enable("false")) multiplexer_2 (
    .in0(O1R0), .in1(O1R1), .in2(O1R2), .in3(O1R3), .in4(O1R4), .in5(O1R5), .in6(O1R6), .in7(O1R7),
    .in8(O1R8), .in9(O1R9), .in10(O1R10), .in11(O1R11), .in12(O1R12), .in13(O1R13), .in14(O1R14),
    .in15(O1R15), .in16(O1R16), .in17(O1R17), .in18(O1R18), .in19(O1R19), .in20(O1R20), .in21(O1R21),
    .in22(O1R22), .in23(O1R23), .in24(O1R24), .in25(O1R25), .in26(O1R26), .in27(O1R27), .in28(O1R28),
    .in29(O1R29), .in30(O1R30), .in31(O1R31), .out(out_8), .sel(rs2));

  // Other names for the same wires on the sheet: I1R0[31:0] = in_1; I1R1[31:0] = in_1; I1R2[31:0] = in_1;
  //   I1R3[31:0] = in_1; I1R4[31:0] = in_1; I1R5[31:0] = in_1; I1R6[31:0] = in_1; I1R7[31:0] = in_1;
  //   I1R8[31:0] = in_1; I1R9[31:0] = in_1; I1R10[31:0] = in_1; I1R11[31:0] = in_1; I1R12[31:0] = in_1;
  //   I1R13[31:0] = in_1; I1R14[31:0] = in_1; I1R15[31:0] = in_1; I1R16[31:0] = in_1; I1R17[31:0] = in_1;
  //   I1R18[31:0] = in_1; I1R19[31:0] = in_1; I1R20[31:0] = in_1; I1R21[31:0] = in_1; I1R22[31:0] = in_1;
  //   I1R23[31:0] = in_1; I1R24[31:0] = in_1; I1R25[31:0] = in_1; I1R26[31:0] = in_1; I1R27[31:0] = in_1;
  //   I1R28[31:0] = in_1; I1R29[31:0] = in_1; I1R30[31:0] = in_1; I1R31[31:0] = in_1
endmodule

module l (
  input  [31:0] in_1,
  input  [4:0] in_2,
  input  [4:0] in_3,
  input  [4:0] in_4,
  input  in_5,
  output [31:0] out_6,
  output [31:0] out_7
);

  wire clock_1_out;

  RegFile regfile_1 (
    .in_1(in_1), .out_7(out_6), .out_8(out_7), .Reg_En(in_5), .dest(in_2), .rs2(in_4), .rs1(in_3),
    .in_2(clock_1_out));
  Clock clock_1 (.out(clock_1_out));
endmodule

// I G
module imm_Gener (
  input  [31:0] in_1,
  input  [1:0] in_2,
  output [31:0] out_3
);

  wire [31:0] bit_extender_1_out, bit_extender_2_out, bit_extender_3_out, shifter_1_out;

  assign bit_extender_1_out = {{12{in_1[31]}}, in_1[31:12]};  // Bit_Extender bit_extender_1
  Shifter #(.width(32)) shifter_1 (.in(bit_extender_1_out), .\dist (5'b01100), .out(shifter_1_out));
  assign bit_extender_2_out = {{20{in_1[31]}}, in_1[31:20]};  // Bit_Extender bit_extender_2
  assign bit_extender_3_out = {{20{in_1[31]}}, {in_1[31:25], in_1[11:7]}};  // Bit_Extender bit_extender_3
  Multiplexer #(.select(2), .width(32), .enable("false")) multiplexer_1 (
    .in0(bit_extender_2_out), .in1(bit_extender_3_out), .in2(shifter_1_out), .in3(bit_extender_1_out),
    .out(out_3), .sel(in_2));
endmodule

// st
module Store (
  input  [31:0] in_1,
  input  [2:0] in_2,
  output [31:0] out_3
);

  wire [31:0] bit_extender_1_out, bit_extender_2_out;

  assign bit_extender_1_out = {{24{in_1[7]}}, in_1[7:0]};  // Bit_Extender bit_extender_1
  assign bit_extender_2_out = {{16{in_1[15]}}, in_1[15:0]};  // Bit_Extender bit_extender_2
  Multiplexer #(.select(3), .width(32), .enable("false")) multiplexer_1 (
    .in0(bit_extender_1_out), .in1(bit_extender_2_out), .in2(in_1), .out(out_3), .sel(in_2));  // open: in3, in4, in5, in6, in7
endmodule

// load
module Load (
  input  [31:0] in_1,
  input  [2:0] in_2,
  output [31:0] out_3
);

  wire [31:0] bit_extender_1_out, bit_extender_2_out, bit_extender_3_out, bit_extender_4_out;

  assign bit_extender_1_out = {{24{in_1[7]}}, in_1[7:0]};  // Bit_Extender bit_extender_1
  assign bit_extender_2_out = {{16{in_1[15]}}, in_1[15:0]};  // Bit_Extender bit_extender_2
  assign bit_extender_3_out = {{24{1'b0}}, in_1[7:0]};  // Bit_Extender bit_extender_3
  assign bit_extender_4_out = {{16{1'b0}}, in_1[15:0]};  // Bit_Extender bit_extender_4
  Multiplexer #(.select(3), .width(32), .enable("false")) multiplexer_1 (
    .in0(bit_extender_1_out), .in1(bit_extender_2_out), .in2(in_1), .in4(bit_extender_3_out),
    .in5(bit_extender_4_out), .out(out_3), .sel(in_2));  // open: in3, in6, in7
endmodule

module branch (
  input  [31:0] in_1,
  input  [31:0] in_2,
  input  [2:0] in_3,
  output out_4
);

  wire comparator_1_eq, comparator_1_gt, comparator_1_lt, comparator_2_eq, comparator_2_gt, comparator_2_lt,
       not_1_out, or_1_out, or_2_out;

  Comparator #(.width(32)) comparator_1 (
    .a(in_1), .b(in_2), .gt(comparator_1_gt), .eq(comparator_1_eq), .lt(comparator_1_lt));
  Comparator #(.width(32), .mode("unsigned")) comparator_2 (
    .a(in_1), .b(in_2), .gt(comparator_2_gt), .eq(comparator_2_eq), .lt(comparator_2_lt));
  not not_1 (not_1_out, comparator_1_eq);
  or or_1 (or_1_out, comparator_1_eq, comparator_1_gt);
  or or_2 (or_2_out, comparator_2_gt, comparator_2_eq);
  Multiplexer #(.select(3), .enable("false")) multiplexer_1 (
    .in0(comparator_1_eq), .in1(not_1_out), .in4(comparator_1_lt), .in5(or_1_out), .in6(comparator_2_lt),
    .in7(or_2_out), .out(out_4), .sel(in_3));  // open: in2, in3
endmodule

module imm_4 (
  input  [11:0] in_1,
  input  [31:0] in_2,
  output [11:0] out_3
);

  Multiplier #(.width(12)) multiplier_1 (.a(in_1), .b(in_2[11:0]), .out(out_3));  // open: cin, cout
endmodule

module CU (
  input  [31:0] in_1
);

  wire comparator_1_eq, comparator_2_eq, mem_out, not_5_out, reg_out, rs1_out, rs2_out;
  wire [1:0] dst_out, not_1_out, not_4_out, not_7_out, not_8_out, pc_4_out;

  assign pc_4_out = not_1_out & not_4_out;  // AND_Gate pc_4, 2 bits wide
  not not_1 (not_1_out[0], comparator_1_eq);
  not not_2 (not_1_out[1], comparator_1_eq);
  Comparator #(.width(7)) comparator_1 (.a(in_1[6:0]), .b(7'b0110011), .eq(comparator_1_eq));  // open: gt, lt
  not not_3 (not_4_out[1], comparator_2_eq);
  not not_4 (not_4_out[0], comparator_2_eq);
  Comparator #(.width(7)) comparator_2 (.a(in_1[6:0]), .b(7'b0010011), .eq(comparator_2_eq));  // open: gt, lt
  or \reg  (reg_out, comparator_1_eq, comparator_2_eq);
  and rs1 (rs1_out, comparator_1_eq, comparator_2_eq);
  and rs2 (rs2_out, comparator_1_eq, not_5_out);
  not not_5 (not_5_out, comparator_2_eq);
  assign dst_out = not_7_out & not_8_out;  // AND_Gate dst, 2 bits wide
  and mem (mem_out, comparator_2_eq, comparator_2_eq);
  not not_6 (not_7_out[1], comparator_1_eq);
  not not_7 (not_7_out[0], comparator_1_eq);
  not not_8 (not_8_out[0], comparator_2_eq);
  not not_9 (not_8_out[1], comparator_2_eq);
endmodule

// OPcodes
module opcodes (
  input  [6:0] in_1,
  input  [2:0] in_2,
  input  [6:0] in_3,
  output out_4,
  output [2:0] out_5,
  output [2:0] out_6,
  output [2:0] out_7,
  output out_8,
  output [2:0] out_9,
  output out_10,
  output out_11,
  output out_12,
  output out_13,
  output out_14,
  output out_15,
  output out_16,
  output Mem,
  output out_18,
  output out_19
);

  wire aui_out, comparator_1_eq, Im_out, jal_out, lui_out, not_1_out, not_2_out, not_3_out, not_4_out,
       not_5_out, not_6_out, not_7_out, not_8_out, not_9_out, not_10_out, not_11_out, not_12_out, not_13_out,
       not_14_out, not_15_out, not_16_out, not_17_out, not_18_out, not_19_out, not_20_out, not_21_out,
       not_22_out, not_23_out, not_24_out, not_25_out, not_26_out, R_out;
  wire [3:0] or_1_out;

  not not_1 (not_1_out, in_1[4]);
  not not_2 (not_2_out, in_1[4]);
  not not_3 (not_3_out, in_1[2]);
  not not_4 (not_4_out, in_1[5]);
  not not_5 (not_5_out, in_1[3]);
  not not_6 (not_6_out, in_1[3]);
  not not_7 (not_7_out, in_1[4]);
  not not_8 (not_8_out, in_1[3]);
  not not_9 (not_9_out, in_1[6]);
  not not_10 (not_10_out, in_1[3]);
  not not_11 (not_11_out, in_1[6]);
  not not_12 (not_12_out, in_1[3]);
  not not_13 (not_13_out, in_1[4]);
  not not_14 (not_14_out, in_1[6]);
  not not_15 (not_15_out, in_1[4]);
  not not_16 (not_16_out, in_1[2]);
  not not_17 (not_17_out, in_1[6]);
  not not_18 (not_18_out, in_1[3]);
  not not_19 (not_19_out, in_1[2]);
  not not_20 (not_20_out, in_1[6]);
  not not_21 (not_21_out, in_1[5]);
  not not_22 (not_22_out, in_1[2]);
  not not_23 (not_23_out, in_1[6]);
  not not_24 (not_24_out, in_1[5]);
  not not_25 (not_25_out, in_1[3]);
  not not_26 (not_26_out, in_1[2]);
  and pc_msb (out_4, in_1[6], in_1[5], not_1_out, in_1[2], in_1[1], in_1[0]);
  and br (or_1_out[3], in_1[6], in_1[5], not_2_out, not_8_out, not_3_out, in_1[1], in_1[0]);
  and lui (lui_out, not_9_out, in_1[5], in_1[4], not_10_out, in_1[2], in_1[1], in_1[0]);
  and aui (aui_out, not_11_out, not_4_out, in_1[4], not_12_out, in_1[2], in_1[1], in_1[0]);
  and jal (jal_out, in_1[6], in_1[5], not_13_out, in_1[3], in_1[2], in_1[1], in_1[0]);
  and S (Mem, not_14_out, in_1[5], not_15_out, not_5_out, not_16_out, in_1[1], in_1[0]);
  and R (R_out, not_17_out, in_1[5], in_1[4], not_18_out, not_19_out, in_1[1], in_1[0]);
  and Im (Im_out, not_20_out, not_21_out, in_1[4], not_6_out, not_22_out, in_1[1], in_1[0]);
  and L (or_1_out[1], not_23_out, not_24_out, not_7_out, not_25_out, not_26_out, in_1[1], in_1[0]);
  or pc_lsb (out_8, out_4, or_1_out[3]);
  or imm_m (out_10, lui_out, aui_out, jal_out);
  or imm_l (out_12, Mem, or_1_out[3], jal_out);
  or RegEn (out_14, out_4, aui_out, lui_out, R_out, Im_out, or_1_out[1]);
  or src2 (out_15, Im_out, Mem, or_1_out[1], or_1_out[3], aui_out, out_4);
  or src1 (out_16, aui_out, or_1_out[3], jal_out);
  or WB_m (out_18, lui_out, out_4);
  or WB_l (out_19, lui_out, or_1_out[1]);
  or or_1 (or_1_out[0], R_out, Im_out);
  Demultiplexer #(.select(4), .width(3), .enable("false")) demultiplexer_1 (
    .out1(out_5), .out2(out_6), .out4(out_7), .out8(out_9), .in(in_2), .sel({or_1_out[3], Mem, or_1_out[1:0]}));  // open: out0, out3, out5, out6, out7, out9, out10, out11, out12, out13, out14, out15
  and and_1 (out_11, in_3[5], R_out);
  Comparator #(.width(3)) comparator_1 (.a(3'b101), .b(in_2), .eq(comparator_1_eq));  // open: gt, lt
  and and_2 (out_13, in_3[5], or_1_out[0], comparator_1_eq);
endmodule

// Control unit
module control (
  input  [31:0] in_1,
  output out_2,
  output [1:0] out_3,
  output out_4,
  output [1:0] out_5,
  output out_6,
  output [1:0] out_7,
  output out_8,
  output out_9,
  output out_10,
  output [2:0] out_11,
  output [2:0] out_12,
  output [2:0] out_13,
  output [2:0] out_14
);

  opcodes opcodes_1 (
    .in_1(in_1[6:0]), .out_4(out_3[1]), .out_8(out_3[0]), .out_10(out_5[1]), .out_12(out_5[0]),
    .out_14(out_2), .out_15(out_8), .out_16(out_9), .Mem(out_10), .out_18(out_7[1]), .out_19(out_7[0]),
    .out_5(out_11), .out_6(out_12), .out_7(out_13), .in_2(in_1[14:12]), .out_9(out_14), .in_3(in_1[31:25]),
    .out_11(out_6), .out_13(out_4));
endmodule
